// Logisim project minirv32.circ as structural Verilog: 6 circuits, main circuit main
module main (
  input  in_1,
  input  in_2
);

  wire clock_1_out, inst_i_dec_1_ramren, inst_s_dec_1_ramwen, or_1_out, or_2_out, priority_encoder_1_p2,
       priority_encoder_1_p3, priority_encoder_1_p4, undriven;
  wire [1:0] priority_encoder_1_p1, priority_encoder_2_out;
  wire [3:0] inst_i_dec_1_gprwaddr, inst_r_dec_1_gprwaddr, inst_u_dec_1_gprwaddr, multiplexer_3_out,
       multiplexer_4_out, multiplexer_5_out;
  wire [7:0] rom_1_data_2;
  wire [11:0] rom_1_data, rom_1_data_3;
  wire [31:0] adder_1_out, gprs_1_q0, gprs_1_q1, inst_i_dec_1_gprwdata, inst_i_dec_1_pcdata,
       inst_r_dec_1_gprwdata, inst_s_dec_1_ramaddr, inst_s_dec_1_ramwdata, inst_u_dec_1_gprwdata,
       multiplexer_1_out, multiplexer_2_out, PC_q, ram_1_dout;

  Clock clock_1 (.out(clock_1_out));
  RAM #(.addrWidth(16), .dataWidth(32), .\type ("nonvolatile")) ram_1 (
    .addr(multiplexer_1_out[15:0]), .we(inst_s_dec_1_ramwen), .oe(inst_i_dec_1_ramren), .clk(clock_1_out),
    .din(inst_s_dec_1_ramwdata), .dout(ram_1_dout));
  Register #(.width(32)) PC (.D(inst_i_dec_1_pcdata), .en(in_1), .clk(clock_1_out), .Q(PC_q), .clr(in_2));
  Adder #(.width(32)) adder_1 (.a(32'h4), .b(PC_q), .out(adder_1_out));  // open: cin, cout
  ROM #(.addrWidth(16), .dataWidth(32)) rom_1 (.addr(PC_q[17:2]), .data({rom_1_data_3, rom_1_data_2, rom_1_data}));
  // Priority_Encoder #(.select(2)) priority_encoder_1: pin names not known; wires that end beside it: priority_encoder_1_p1, priority_encoder_1_p2, priority_encoder_1_p3, priority_encoder_1_p4, 1'b0
  Inst_I_dec inst_i_dec_1 (
    .opc(rom_1_data[6:0]), .rdaddr(rom_1_data[11:7]), .funct3(rom_1_data_2[2:0]),
    .rs1addr(rom_1_data_2[7:3]), .imm(rom_1_data_3), .rs1data(gprs_1_q0), .PCplus4(adder_1_out),
    .RAMdata(ram_1_dout), .GPRwe(priority_encoder_1_p2), .GPRwaddr(inst_i_dec_1_gprwaddr),
    .RAMren(inst_i_dec_1_ramren), .GPRwdata(inst_i_dec_1_gprwdata), .PCdata(inst_i_dec_1_pcdata));  // open: GPRraddr0, RAMaddr
  Inst_R_dec inst_r_dec_1 (
    .opc(rom_1_data[6:0]), .rdaddr(rom_1_data[11:7]), .funct3(rom_1_data_2[2:0]),
    .rs1addr(rom_1_data_2[7:3]), .rs2addr(rom_1_data_3[4:0]), .funct7(rom_1_data_3[11:5]),
    .rs1data(gprs_1_q0), .rs2data(gprs_1_q1), .GPRwe(priority_encoder_1_p3),
    .GPRwaddr(inst_r_dec_1_gprwaddr), .GPRwdata(inst_r_dec_1_gprwdata));  // open: GPRraddr0, GPRraddr1
  Inst_U_dec inst_u_dec_1 (
    .opc(rom_1_data[6:0]), .rdaddr(rom_1_data[11:7]), .imm({rom_1_data_3, rom_1_data_2}),
    .GPRwe(priority_encoder_1_p4), .GPRwaddr(inst_u_dec_1_gprwaddr), .GPRwdata(inst_u_dec_1_gprwdata));
  Inst_S_dec inst_s_dec_1 (
    .opc(rom_1_data[6:0]), .imm0to4(rom_1_data[11:7]), .funct3(rom_1_data_2[2:0]),
    .rs1addr(rom_1_data_2[7:3]), .rs2addr(rom_1_data_3[4:0]), .imm5to11(rom_1_data_3[11:5]),
    .rs1data(gprs_1_q0), .rs2data(gprs_1_q1), .RAMwen(inst_s_dec_1_ramwen), .RAMaddr(inst_s_dec_1_ramaddr),
    .RAMwdata(inst_s_dec_1_ramwdata));  // open: GPRraddr0, GPRraddr1
  Multiplexer #(.enable("true"), .width(32)) multiplexer_1 (
    .in0(inst_s_dec_1_ramaddr), .out(multiplexer_1_out), .sel(inst_i_dec_1_ramren), .en(or_1_out));  // open: in1
  or or_1 (or_1_out, inst_i_dec_1_ramren, inst_s_dec_1_ramwen);
  Priority_Encoder #(.select(2)) priority_encoder_2 (.out(priority_encoder_2_out));  // open: in0, in1, in2, in3, gs, en_out, en_in
  or or_2 (or_2_out, priority_encoder_1_p2, priority_encoder_1_p3, priority_encoder_1_p4);
  Multiplexer #(.enable("true"), .select(2), .width(32)) multiplexer_2 (
    .in0(inst_i_dec_1_gprwdata), .in1(inst_r_dec_1_gprwdata), .in2(inst_u_dec_1_gprwdata),
    .out(multiplexer_2_out), .sel(priority_encoder_1_p1), .en(or_2_out));  // open: in3
  Multiplexer #(.enable("true"), .select(2), .width(4)) multiplexer_3 (
    .in0(inst_i_dec_1_gprwaddr), .in1(inst_r_dec_1_gprwaddr), .in2(inst_u_dec_1_gprwaddr),
    .out(multiplexer_3_out), .sel(priority_encoder_1_p1), .en(or_2_out));  // open: in3
  Multiplexer #(.select(2), .width(4)) multiplexer_4 (.out(multiplexer_4_out));  // open: in0, in1, in2, in3, sel
  Multiplexer #(.width(4)) multiplexer_5 (.out(multiplexer_5_out));  // open: in0, in1, sel
  GPRs gprs_1 (
    .clk(clock_1_out), .wdata(multiplexer_2_out), .waddr(multiplexer_3_out), .WE(or_2_out),
    .raddr0(multiplexer_4_out), .raddr1(multiplexer_5_out), .RST(undriven), .Q0(gprs_1_q0), .Q1(gprs_1_q1));

  // Notes on the sheet:
  //   contents of rom_1 (hex, n*v repeats v):
  //   1400513 10000e7 c000e7 c00067 a50513 8067
endmodule

module GPRs (
  input  clk,
  input  [31:0] wdata,
  input  [3:0] waddr,
  input  WE,
  input  [3:0] raddr0,
  input  [3:0] raddr1,
  input  RST,
  output [31:0] Q0,
  output [31:0] Q1
);

  wire decoder_1_out1, decoder_1_out2, decoder_1_out3, decoder_1_out4, decoder_1_out5, decoder_1_out6,
       decoder_1_out7, decoder_1_out8, decoder_1_out9, decoder_1_out10, decoder_1_out11, decoder_1_out12,
       decoder_1_out13, decoder_1_out14, decoder_1_out15;
  wire [31:0] register_1_q, register_2_q, register_3_q, register_4_q, register_5_q, register_6_q,
       register_7_q, register_8_q, register_9_q, register_10_q, register_11_q, register_12_q, register_13_q,
       register_14_q, register_15_q;

  Decoder #(.select(4)) decoder_1 (
    .out1(decoder_1_out1), .out2(decoder_1_out2), .out3(decoder_1_out3), .out4(decoder_1_out4),
    .out5(decoder_1_out5), .out6(decoder_1_out6), .out7(decoder_1_out7), .out8(decoder_1_out8),
    .out9(decoder_1_out9), .out10(decoder_1_out10), .out11(decoder_1_out11), .out12(decoder_1_out12),
    .out13(decoder_1_out13), .out14(decoder_1_out14), .out15(decoder_1_out15), .sel(waddr), .en(WE));  // open: out0
  Register #(.width(32)) register_1 (.D(wdata), .en(decoder_1_out8), .clk(clk), .Q(register_1_q), .clr(RST));
  Register #(.width(32)) register_2 (.D(wdata), .en(decoder_1_out1), .clk(clk), .Q(register_2_q), .clr(RST));
  Register #(.width(32)) register_3 (.D(wdata), .en(decoder_1_out9), .clk(clk), .Q(register_3_q), .clr(RST));
  Register #(.width(32)) register_4 (.D(wdata), .en(decoder_1_out2), .clk(clk), .Q(register_4_q), .clr(RST));
  Register #(.width(32)) register_5 (.D(wdata), .en(decoder_1_out10), .clk(clk), .Q(register_5_q), .clr(RST));
  Register #(.width(32)) register_6 (.D(wdata), .en(decoder_1_out3), .clk(clk), .Q(register_6_q), .clr(RST));
  Register #(.width(32)) register_7 (.D(wdata), .en(decoder_1_out11), .clk(clk), .Q(register_7_q), .clr(RST));
  Register #(.width(32)) register_8 (.D(wdata), .en(decoder_1_out4), .clk(clk), .Q(register_8_q), .clr(RST));
  Register #(.width(32)) register_9 (.D(wdata), .en(decoder_1_out12), .clk(clk), .Q(register_9_q), .clr(RST));
  Register #(.width(32)) register_10 (.D(wdata), .en(decoder_1_out5), .clk(clk), .Q(register_10_q), .clr(RST));
  Register #(.width(32)) register_11 (.D(wdata), .en(decoder_1_out13), .clk(clk), .Q(register_11_q), .clr(RST));
  Register #(.width(32)) register_12 (.D(wdata), .en(decoder_1_out6), .clk(clk), .Q(register_12_q), .clr(RST));
  Register #(.width(32)) register_13 (.D(wdata), .en(decoder_1_out14), .clk(clk), .Q(register_13_q), .clr(RST));
  Register #(.width(32)) register_14 (.D(wdata), .en(decoder_1_out7), .clk(clk), .Q(register_14_q), .clr(RST));
  Register #(.width(32)) register_15 (.D(wdata), .en(decoder_1_out15), .clk(clk), .Q(register_15_q), .clr(RST));
  Multiplexer #(.select(4), .width(32)) multiplexer_1 (
    .in0({32{1'b0}}), .in1(register_2_q), .in2(register_4_q), .in3(register_6_q), .in4(register_8_q),
    .in5(register_10_q), .in6(register_12_q), .in7(register_14_q), .in8(register_1_q), .in9(register_3_q),
    .in10(register_5_q), .in11(register_7_q), .in12(register_9_q), .in13(register_11_q),
    .in14(register_13_q), .in15(register_15_q), .out(Q0), .sel(raddr0));
  Multiplexer #(.select(4), .width(32)) multiplexer_2 (
    .in0({32{1'b0}}), .in1(register_2_q), .in2(register_4_q), .in3(register_6_q), .in4(register_8_q),
    .in5(register_10_q), .in6(register_12_q), .in7(register_14_q), .in8(register_1_q), .in9(register_3_q),
    .in10(register_5_q), .in11(register_7_q), .in12(register_9_q), .in13(register_11_q),
    .in14(register_13_q), .in15(register_15_q), .out(Q1), .sel(raddr1));
endmodule

module Inst_I_dec (
  input  [6:0] opc,
  input  [4:0] rdaddr,
  input  [2:0] funct3,
  input  [4:0] rs1addr,
  input  [11:0] imm,
  input  [31:0] rs1data,
  input  [31:0] PCplus4,
  input  [31:0] RAMdata,
  output GPRwe,
  output [3:0] GPRwaddr,
  output [3:0] GPRraddr0,
  output [31:0] RAMaddr,
  output RAMren,
  output [31:0] GPRwdata,
  output [31:0] PCdata
);

  wire addi_out, comparator_1_eq, comparator_2_eq, comparator_3_eq, comparator_4_eq, comparator_5_eq,
       comparator_6_eq, jalr_out, lbu_out, lw_out;
  wire [31:0] adder_1_out, bit_extender_1_out;

  Comparator #(.width(7)) comparator_1 (.a(opc), .b(7'b0010011), .eq(comparator_1_eq));  // open: gt, lt
  Comparator #(.width(7)) comparator_2 (.a(opc), .b(7'b1100111), .eq(comparator_2_eq));  // open: gt, lt
  Comparator #(.width(7)) comparator_3 (.a(opc), .b(7'b0000011), .eq(comparator_3_eq));  // open: gt, lt
  Comparator #(.width(3)) comparator_4 (.a(funct3), .b(3'b000), .eq(comparator_4_eq));  // open: gt, lt
  Comparator #(.width(3)) comparator_5 (.a(funct3), .b(3'b100), .eq(comparator_5_eq));  // open: gt, lt
  Comparator #(.width(3)) comparator_6 (.a(funct3), .b(3'b010), .eq(comparator_6_eq));  // open: gt, lt
  assign bit_extender_1_out = {{20{imm[11]}}, imm};  // Bit_Extender bit_extender_1
  Adder #(.width(32)) adder_1 (.a(bit_extender_1_out), .b(rs1data), .out(adder_1_out));  // open: cin, cout
  and addi (addi_out, comparator_1_eq, comparator_4_eq);
  and jalr (jalr_out, comparator_2_eq, comparator_4_eq);
  and lbu (lbu_out, comparator_5_eq, comparator_3_eq);
  and lw (lw_out, comparator_3_eq, comparator_6_eq);
  Multiplexer #(.width(32)) multiplexer_1 (.in0(adder_1_out), .in1(PCplus4), .out(RAMaddr), .sel(jalr_out));
  Multiplexer #(.width(32)) multiplexer_2 (.in0(PCplus4), .in1(adder_1_out), .out(PCdata), .sel(jalr_out));
  or or_1 (GPRwe, addi_out, jalr_out, lbu_out, lw_out);
  or LS (RAMren, lw_out, lbu_out);
  Multiplexer #(.width(32)) multiplexer_3 (.in0(RAMaddr), .in1(RAMdata), .out(GPRwdata), .sel(RAMren));

  assign GPRraddr0 = rs1addr[3:0];
  assign GPRwaddr = rdaddr[3:0];
endmodule

module Inst_R_dec (
  input  [6:0] opc,
  input  [4:0] rdaddr,
  input  [2:0] funct3,
  input  [4:0] rs1addr,
  input  [4:0] rs2addr,
  input  [6:0] funct7,
  input  [31:0] rs1data,
  input  [31:0] rs2data,
  output GPRwe,
  output [3:0] GPRwaddr,
  output [3:0] GPRraddr0,
  output [3:0] GPRraddr1,
  output [31:0] GPRwdata
);

  wire comparator_1_eq, comparator_2_eq, comparator_3_eq;

  Comparator #(.width(7)) comparator_1 (.a(opc), .b(7'b0110011), .eq(comparator_1_eq));  // open: gt, lt
  Comparator #(.width(3)) comparator_2 (.a(funct3), .b(3'b000), .eq(comparator_2_eq));  // open: gt, lt
  Comparator #(.width(7)) comparator_3 (.a(funct7), .b({7{1'b0}}), .eq(comparator_3_eq));  // open: gt, lt
  Adder #(.width(32)) adder_1 (.a(rs1data), .b(rs2data), .out(GPRwdata));  // open: cin, cout
  and and_1 (GPRwe, comparator_1_eq, comparator_2_eq, comparator_3_eq);

  assign GPRraddr0 = rs1addr[3:0];
  assign GPRraddr1 = rs2addr[3:0];
  assign GPRwaddr = rdaddr[3:0];
endmodule

module Inst_U_dec (
  input  [6:0] opc,
  input  [4:0] rdaddr,
  input  [19:0] imm,
  output GPRwe,
  output [3:0] GPRwaddr,
  output [31:0] GPRwdata
);

  Comparator #(.width(7)) comparator_1 (.a(opc), .b(7'b0110111), .eq(GPRwe));  // open: gt, lt

  assign GPRwaddr = rdaddr[3:0];
  assign GPRwdata = {imm, {12{1'b0}}};
endmodule

module Inst_S_dec (
  input  [6:0] opc,
  input  [4:0] imm0to4,
  input  [2:0] funct3,
  input  [4:0] rs1addr,
  input  [4:0] rs2addr,
  input  [6:0] imm5to11,
  input  [31:0] rs1data,
  input  [31:0] rs2data,
  output RAMwen,
  output [3:0] GPRraddr0,
  output [3:0] GPRraddr1,
  output [31:0] RAMaddr,
  output [31:0] RAMwdata
);

  wire comparator_1_eq, comparator_2_eq, comparator_3_eq, sb_out, sw_out;
  wire [31:0] bit_extender_1_out;

  Comparator #(.width(7)) comparator_1 (.a(opc), .b(7'b0100011), .eq(comparator_1_eq));  // open: gt, lt
  Comparator #(.width(3)) comparator_2 (.a(funct3), .b(3'b000), .eq(comparator_2_eq));  // open: gt, lt
  Comparator #(.width(3)) comparator_3 (.a(3'b001), .b(funct3), .eq(comparator_3_eq));  // open: gt, lt
  assign bit_extender_1_out = {{20{imm5to11[6]}}, {imm5to11, imm0to4}};  // Bit_Extender bit_extender_1
  and sb (sb_out, comparator_1_eq, comparator_2_eq);
  and sw (sw_out, comparator_1_eq, comparator_3_eq);
  Adder #(.width(32)) adder_1 (.a(bit_extender_1_out), .b(rs1data), .out(RAMaddr));  // open: cin, cout
  or or_1 (RAMwen, sb_out, sw_out);

  assign GPRraddr0 = rs1addr[3:0];
  assign GPRraddr1 = rs2addr[3:0];
  assign RAMwdata = rs2data;
endmodule
